# Fritzing sketch shift_lights (saved by Fritzing 0.7.10b)
breadboards: 1

parts:
  Arduino1 = Arduino
  HEF1 = HEF4094 [package="DIP16 [THT]"]
  HEF2 = HEF4094 [package="DIP16 [THT]"]
  LED1 = LED - 5mm [color="Red (633nm)" package="5 mm [THT]"]
  LED2 = LED - 5mm [color="Red (633nm)" package="5 mm [THT]"]
  LED3 = LED - 5mm [color="Red (633nm)" package="5 mm [THT]"]
  LED4 = LED - 5mm [color="Red (633nm)" package="5 mm [THT]"]
  LED5 = LED - 5mm [color="Red (633nm)" package="5 mm [THT]"]
  LED6 = LED - 5mm [color="Red (633nm)" package="5 mm [THT]"]
  LED7 = LED - 5mm [color="Red (633nm)" package="5 mm [THT]"]
  LED8 = LED - 5mm [color="Red (633nm)" package="5 mm [THT]"]
  LED9 = LED - 5mm [color="Red (633nm)" package="5 mm [THT]"]
  LED10 = LED - 5mm [color="Red (633nm)" package="5 mm [THT]"]
  R1 = Resistor [tolerance=±5% resistance=220 package=THT]

nets:
  VSS: Arduino1.GND, HEF1.Vss, HEF2.Vss, R1.Pin_0
  N1: Arduino1.D13, HEF1.DATA
  N2: Arduino1.D12, HEF1.STROBE, HEF2.STROBE
  N3: Arduino1.D11, HEF1.CLOCK, HEF2.CLOCK
  VDD: Arduino1.+5V, HEF1.OE, HEF1.Vdd, HEF2.OE, HEF2.Vdd
  N4: HEF1.Q1, LED10.anode
  N5: HEF1.Q2, LED9.anode
  N6: HEF1.Q3, LED8.anode
  N7: HEF1.Q4, LED7.anode
  N8: HEF1.Qs, HEF2.DATA
  N9: HEF1.Q8, LED3.anode
  N10: HEF1.Q7, LED4.anode
  N11: HEF1.Q6, LED5.anode
  N12: HEF1.Q5, LED6.anode
  N13: HEF2.Q1, LED2.anode
  N14: HEF2.Q2, LED1.anode
  N15: LED1.cathode, LED2.cathode, LED3.cathode, LED4.cathode, LED5.cathode, LED6.cathode, LED7.cathode, LED8.cathode, LED9.cathode, LED10.cathode, R1.Pin_1
